# Fritzing sketch PSoC 4 Pioneer Kit & Sequencer Board & AQM1602 & MCP4922 (saved by Fritzing 0.9.2b)
perfboards: 2
breadboards: 2

parts:
  J1 = female pin header, 5 pins [form="♀ (female)"]
  J2 = female pin header, 8 pins [form="♀ (female)"]
  J3 = double row female pin header, 10 pins [form="♀ (female)"]  # not connected
  J4 = female pin header, 8 pins [form="♀ (female)"]  # not connected
  J5 = female pin header, 10 pins [form="♀ (female)"]
  J6 = female pin header, 6 pins [form="♀ (female)"]  # not connected
  J7 = female pin header, 6 pins [form="♀ (female)"]  # not connected
  R1 = Resistor [tolerance=±5% resistance=10k package=THT]
  U1 = mystery part, 4 pins [chip_label=AQM1602]
  R2 = Resistor [tolerance=±5% resistance=10k package=THT]
  U2 = mystery part, 14 pins [chip_label=MCP4922]
  R3 = Resistor [tolerance=±5% resistance=220 package=THT]
  LED1 = LED - 5mm [color="Red (633nm)" package="5 mm [THT]"]

nets:
  N1: J1.pin1, J2.pin6, U1.pin1, U2.pin12, LED1.cathode
  N2: J1.pin2, J2.pin4, R1.Pin_0, U1.pin4, R2.Pin_0, U2.pin1, U2.pin9, U2.pin11, U2.pin13
  N3: J1.pin3, J5.pin5
  N4: J1.pin4, J5.pin1, R1.Pin_1, U1.pin3
  N5: J1.pin5, J5.pin2, U1.pin2, R2.Pin_1
  N6: U2.pin14, R3.Pin_1
  N7: R3.Pin_0, LED1.anode

notes:
  PSoC 4 Pioneer Kit
  3.3V Drive
  Sequencer Board
