# Fritzing sketch Rythm_Machine_全体案_ver.2 (saved by Fritzing 0.9.2b)
perfboards: 4

parts:
  S1 = Pushbutton [package="[THT]"]
  S2 = Pushbutton [package="[THT]"]
  S3 = Pushbutton [package="[THT]"]
  S4 = Pushbutton [package="[THT]"]
  S5 = Pushbutton [package="[THT]"]
  S6 = Pushbutton [package="[THT]"]
  S7 = Pushbutton [package="[THT]"]
  S8 = Pushbutton [package="[THT]"]
  S9 = Pushbutton [package="[THT]"]
  LED1 = LED - 3mm [color="Red (633nm)" package="3 mm [THT]"]  # not connected
  LED2 = LED - 3mm [color="Red (633nm)" package="3 mm [THT]"]  # not connected
  LED3 = LED - 3mm [color="Red (633nm)" package="3 mm [THT]"]  # not connected
  LED4 = LED - 3mm [color="Red (633nm)" package="3 mm [THT]"]  # not connected
  LED5 = LED - 3mm [color="Red (633nm)" package="3 mm [THT]"]  # not connected
  LED6 = LED - 3mm [color="Red (633nm)" package="3 mm [THT]"]  # not connected
  LED7 = LED - 3mm [color="Red (633nm)" package="3 mm [THT]"]  # not connected
  LED8 = LED - 3mm [color="Red (633nm)" package="3 mm [THT]"]  # not connected
  LED9 = LED - 3mm [color="Blue (525nm)" package="3 mm [THT]"]  # not connected
  LED10 = LED - 3mm [color="Red (633nm)" package="3 mm [THT]"]  # not connected
  R1 = Rotary Potentiometer (Small) [maximum_resistance=100kΩ package=THT]  # not connected
  R2 = Rotary Potentiometer (Small) [maximum_resistance=100kΩ package=THT]  # not connected
  LED11 = LED - 3mm [color="Red (633nm)" package="3 mm [THT]"]  # not connected
  LED12 = LED - 3mm [color="Blue (525nm)" package="3 mm [THT]"]  # not connected
  LED13 = LED - 3mm [color="Blue (525nm)" package="3 mm [THT]"]  # not connected
  J1 = female pin header, 5 pins [form="♀ (female)"]
  U3 = LCD-16X2 [package=lcd-8x2-kit]  # not connected
  J6 = female pin header, 7 pins [form="♀ (female)"]  # not connected
  J7 = female pin header, 7 pins [form="♀ (female)"]  # not connected
  J8 = female pin header, 22 pins [form="♀ (female)"]
  J9 = female pin header, 22 pins [form="♀ (female)"]
  IC1 = Dual Op-Amp [package=dip08]  # not connected
  IC2 = IC, DIP package, 14 pins [chip_label=DAC]  # not connected
  J10 = female pin header, 2 pins [form="♀ (female)"]
  RE1 = Rotary Encoder [package=THT]  # not connected
  JP1 = RCA [package=rca_lock]  # not connected
  J13 = female pin header, 2 pins [form="♀ (female)"]
  U4 = atmega168 [package=dip]  # not connected
  VCC1 = Battery
  J5 = female pin header, 3 pins [form="♀ (female)"]
  J12 = female pin header, 4 pins [form="♀ (female)"]
  RE2 = Rotary Encoder [package=THT]  # not connected
  RE3 = Rotary Encoder [package=THT]  # not connected

nets:
  N1: S1.Pin_1, S1.Pin_2
  N2: S1.Pin_3, S1.Pin_4
  N3: S2.Pin_1, S2.Pin_2
  N4: S2.Pin_3, S2.Pin_4
  N5: S3.Pin_1, S3.Pin_2
  N6: S3.Pin_3, S3.Pin_4
  N7: S4.Pin_1, S4.Pin_2
  N8: S4.Pin_3, S4.Pin_4
  N9: S5.Pin_1, S5.Pin_2
  N10: S5.Pin_3, S5.Pin_4
  N11: S6.Pin_1, S6.Pin_2
  N12: S6.Pin_3, S6.Pin_4
  N13: S7.Pin_1, S7.Pin_2
  N14: S7.Pin_3, S7.Pin_4
  N15: S8.Pin_1, S8.Pin_2
  N16: S8.Pin_3, S8.Pin_4
  N17: S9.Pin_1, S9.Pin_2
  N18: S9.Pin_3, S9.Pin_4
  N19: J1.pin1, J9.pin21, J10.pin1, J13.pin1
  N20: J1.pin2, J9.pin22, J10.pin2, J13.pin2
  N21: J1.pin3, J9.pin14
  N22: J1.pin4, J9.pin10
  N23: J1.pin5, J9.pin11
  N24: J8.pin1, VCC1.-
  N25: J8.pin2, VCC1.+
  N26: J8.pin13, J12.pin1
  N27: J8.pin14, J12.pin2
  N28: J8.pin15, J12.pin3
  N29: J8.pin16, J12.pin4
  N30: J8.pin18, J5.pin1
  N31: J8.pin21, J5.pin2
  N32: J8.pin22, J5.pin3

notes:
  2)I2C
  Sequencer Board
  1') I2C
  Graphic or Charcter LCD
  3)SPI
  DAC & LPF
  1) PSoC 4 Prototyping Kit
  6) Pwr Supply
  3.3V
