# Fritzing sketch CQ_PSoC5LP & Sequencer Board & HD44780 REx3_Recover (saved by Fritzing 0.9.2b)
perfboards: 2
breadboards: 2

parts:
  J1 = female pin header, 5 pins [form="♀ (female)"]
  RE3 = Rotary Encoder [package=THT]
  J9 = female pin header, 20 pins [form="♀ (female)"]
  J10 = female pin header, 20 pins [form="♀ (female)"]
  J11 = female pin header, 20 pins [form="♀ (female)"]
  J12 = female pin header, 20 pins [form="♀ (female)"]
  LCD1 = LCD screen
  R1 = Resistor [tolerance=±5% resistance=220 package=THT]
  R2 = TRIMPOT [package=3362u-2]
  RE4 = Rotary Encoder [package=THT]
  RE5 = Rotary Encoder [package=THT]
  LED1 = RGB LED (com. cathode, rgb) [package="5 mm [THT]"]
  R3 = Resistor [tolerance=±5% resistance=1.5k package=THT]
  R4 = Resistor [tolerance=±5% resistance=1k package=THT]
  R5 = Resistor [tolerance=±5% resistance=1k package=THT]
  R6 = Resistor [tolerance=±5% resistance=10k package=THT]
  R7 = Resistor [tolerance=±5% resistance=10k package=THT]

nets:
  N1: J1.pin1, J9.pin19
  N2: J1.pin2, J10.pin19, R6.Pin_0, R7.Pin_0
  N3: J1.pin3, J9.pin2
  N4: J1.pin4, J9.pin3, R6.Pin_1
  N5: J1.pin5, J10.pin3, R7.Pin_1
  N6: RE3.EncoderPinA, J12.pin9
  N7: RE3.EncoderPinC, J11.pin19, LCD1.VSS, LCD1.LED-, R2.CCW, RE4.EncoderPinC, RE5.EncoderPinC, LED1.green_anode
  N8: RE3.EncoderPinB, J11.pin9
  N9: J9.pin16, R4.Pin_0
  N10: J9.pin17, R5.Pin_0
  N11: J10.pin17, R3.Pin_0
  N12: J11.pin1, LCD1.DB4
  N13: J11.pin2, LCD1.DB6
  N14: J11.pin3, LCD1.E
  N15: J11.pin4, LCD1.R/W
  N16: J11.pin10, RE4.EncoderPinB
  N17: J12.pin1, LCD1.DB5
  N18: J12.pin2, LCD1.DB7
  N19: J12.pin3, LCD1.RS
  N20: J12.pin10, RE4.EncoderPinA
  N21: J12.pin16, RE5.EncoderPinA
  N22: J12.pin19, LCD1.VDD, R1.Pin_0, R2.CW
  N23: LCD1.V0, R2.WIPER
  N24: LCD1.LED+, R1.Pin_1
  N25: LED1.red_anode, R3.Pin_1
  N26: LED1.common_cathode, R4.Pin_1
  N27: LED1.blue_anode, R5.Pin_1

notes:
  Sequencer Board
  1 GND
  2 VCC
  3 Reset
  4 SCL
  5 SDA
  ISR
  TimerTC
  HD44780
  1 VSS 9 D2
  2 VDD 10 D3
  3 V0 11 D4
  4 RS 12 D5
  5 RW 13 D6
  6 E 14 D7
  7 D0 15 LEDA
  8 D1 16 LEDK
