# Fritzing sketch CQ_PSoC5LP & Sequencer Board & SPLC792 & MCP4922 & REx3 - コピー (saved by Fritzing 0.9.2b)
perfboards: 2
breadboards: 2

parts:
  J1 = female pin header, 5 pins [form="♀ (female)"]
  U2 = mystery part, 14 pins [chip_label=MCP4922]
  R3 = Resistor [tolerance=±5% resistance=220 package=THT]
  LED1 = LED - 5mm [color="Red (633nm)" package="5 mm [THT]"]
  C1 = Ceramic Capacitor [capacitance=100nF package="100 mil [THT, multilayer]"]
  C2 = Electrolytic Capacitor [capacitance=1µF package="100 mil [THT, electrolytic]"]
  R4 = Resistor [tolerance=±5% resistance=220 package=THT]
  RE2 = Rotary Encoder [package=THT]
  RE1 = Rotary Encoder [package=THT]
  RE3 = Rotary Encoder [package=THT]
  U1 = mystery part, 9 pins [chip_label=SPLC792]
  J9 = female pin header, 20 pins [form="♀ (female)"]
  J10 = female pin header, 20 pins [form="♀ (female)"]
  J11 = female pin header, 20 pins [form="♀ (female)"]
  J12 = female pin header, 20 pins [form="♀ (female)"]
  R5 = Resistor [tolerance=±5% resistance=1k package=THT]
  R6 = Resistor [tolerance=±5% resistance=1k package=THT]
  R7 = Resistor [tolerance=±5% resistance=1k package=THT]  # not connected

nets:
  N1: J1.pin1, U2.pin12, LED1.cathode, C1.0, C2.-, J9.pin20
  N2: J1.pin2, U2.pin1, U2.pin9, U2.pin11, U2.pin13, C1.1, C2.+, J10.pin19
  N3: J1.pin3, J11.pin2
  N4: J1.pin4, J12.pin1
  N5: J1.pin5, J11.pin1
  N6: U2.pin3, J9.pin9
  N7: U2.pin4, J10.pin10
  N8: U2.pin5, J9.pin10
  N9: U2.pin8, J10.pin9
  N10: U2.pin14, R3.Pin_1
  N11: R3.Pin_0, LED1.anode
  N12: R4.Pin_0, U1.pin9, J12.pin19
  N13: R4.Pin_1, U1.pin1
  N14: RE2.EncoderPinA, J12.pin10
  N15: RE2.EncoderPinC, RE1.EncoderPinC, RE3.EncoderPinC, U1.pin2, U1.pin6, J11.pin19
  N16: RE2.EncoderPinB, J11.pin10
  N17: RE1.EncoderPinA, J12.pin9
  N18: RE1.EncoderPinB, J11.pin9
  N19: RE3.EncoderPinA, J12.pin13
  N20: RE3.EncoderPinB, J11.pin13
  N21: U1.pin3, J11.pin7
  N22: U1.pin4, J12.pin6
  N23: U1.pin5, J11.pin6
  N24: J11.pin17, R5.Pin_0
  N25: J12.pin17, R6.Pin_0

notes:
  Sequencer Board
  MCP4922
  1 VDD 8 ~LDAC
  2 NC 9 ~SHDN
  3 ~CS 10 VOUTB
  4 SCK 11 VREFB
  5 SDI 12 AVSS
  6 NC 13 VREFA
  7 NC 14 VOUTA
  ISR
  TimerTC
