# Fritzing sketch PSoC 5LP Prototyping Kit & Sequencer Board & HD44780 REx3 (saved by Fritzing 0.9.2b)
perfboards: 1
breadboards: 3

parts:
  J1 = female pin header, 5 pins [form="♀ (female)"]
  RE3 = Rotary Encoder [package=THT]
  LCD1 = LCD screen
  R1 = Resistor [tolerance=±5% resistance=220 package=THT]
  R2 = TRIMPOT [package=3362u-2]
  RE4 = Rotary Encoder [package=THT]
  RE5 = Rotary Encoder [package=THT]
  LED1 = RGB LED (com. cathode, rgb) [package="5 mm [THT]"]
  R3 = Resistor [tolerance=±5% resistance=1.5k package=THT]
  R4 = Resistor [tolerance=±5% resistance=1k package=THT]
  R5 = Resistor [tolerance=±5% resistance=1k package=THT]
  R6 = Resistor [tolerance=±5% resistance=10k package=THT]
  R7 = Resistor [tolerance=±5% resistance=10k package=THT]
  U1 = mystery part, 52 pins [chip_label="PSoC 5LP Prototyping Kit"]

nets:
  N1: J1.pin1, U1.pin51
  N2: J1.pin2, R6.Pin_0, R7.Pin_0, U1.pin36, U1.pin37, U1.pin52
  N3: J1.pin3, U1.pin45
  N4: J1.pin4, R6.Pin_1, U1.pin43
  N5: J1.pin5, R7.Pin_1, U1.pin44
  N6: RE3.EncoderPinC, LCD1.VSS, LCD1.LED-, R2.CCW, RE4.EncoderPinC, RE5.EncoderPinC, LED1.green_anode, U1.pin25
  N7: LCD1.VDD, R1.Pin_0, R2.CW, U1.pin26
  N8: LCD1.V0, R2.WIPER
  N9: LCD1.RS, U1.pin6
  N10: LCD1.R/W, U1.pin7
  N11: LCD1.E, U1.pin5
  N12: LCD1.DB4, U1.pin1
  N13: LCD1.DB5, U1.pin2
  N14: LCD1.DB6, U1.pin3
  N15: LCD1.DB7, U1.pin4
  N16: LCD1.LED+, R1.Pin_1
  N17: LED1.red_anode, R3.Pin_1
  N18: LED1.common_cathode, R4.Pin_1
  N19: LED1.blue_anode, R5.Pin_1
  N20: R3.Pin_0, U1.pin23
  N21: R4.Pin_0, U1.pin24
  N22: R5.Pin_0, U1.pin22

notes:
  Sequencer Board
  1 GND
  2 VCC
  3 Reset
  4 SCL
  5 SDA
  ISR
  TimerTC
  HD44780
  1 VSS 9 D2
  2 VDD 10 D3
  3 V0 11 D4
  4 RS 12 D5
  5 RW 13 D6
  6 E 14 D7
  7 D0 15 LEDA
  8 D1 16 LEDK
