# Fritzing sketch Rhythm Machine Master PSoC 5LP Prototyping Kit (saved by Fritzing 0.9.2b)
breadboards: 3
perfboards: 2

parts:
  U1 = mystery part, 52 pins [chip_label="PSoC 5LP Prototyping Kit"]
  LCD1 = LCD screen
  R1 = TRIMPOT [package=3362u-2]
  R2 = Resistor [tolerance=±5% resistance=1k package=THT]
  R3 = Resistor [tolerance=±5% resistance=1k package=THT]
  R4 = Resistor [tolerance=±5% resistance=1.5k package=THT]
  LED1 = RGB LED (com. cathode, rgb) [package="5 mm [THT]"]
  J1 = female pin header, 5 pins [form="♀ (female)"]
  R5 = Resistor [tolerance=±5% resistance=10k package=THT]
  R6 = Resistor [tolerance=±5% resistance=10k package=THT]
  S1 = Pushbutton [package="[THT]"]
  S2 = Pushbutton [package="[THT]"]
  S3 = Pushbutton [package="[THT]"]
  S4 = Pushbutton [package="[THT]"]
  SPKR1 = Loudspeaker
  R7 = Resistor [tolerance=±5% resistance=1k package=THT]
  RE2 = Rotary Encoder [package=THT]
  RE3 = Rotary Encoder [package=THT]
  RE1 = Rotary Encoder [package=THT]
  C1 = Electrolytic Capacitor [capacitance=1µF package="100 mil [THT, electrolytic]"]
  R8 = Resistor [tolerance=±5% resistance=1k package=THT]
  LED2 = LED - 3mm [color="Red (633nm)" package="3 mm [THT]"]

nets:
  N1: U1.pin1, LCD1.DB4
  N2: U1.pin2, LCD1.DB5
  N3: U1.pin3, LCD1.DB6
  N4: U1.pin4, LCD1.DB7
  N5: U1.pin5, LCD1.E
  N6: U1.pin6, LCD1.RS
  N7: U1.pin7, LCD1.R/W
  N8: U1.pin9, R4.Pin_0
  N9: U1.pin10, R2.Pin_0
  N10: U1.pin11, R3.Pin_0
  N11: U1.pin22, J1.pin3
  N12: U1.pin23, J1.pin2, R6.Pin_0
  N13: U1.pin24, J1.pin1, R5.Pin_0
  N14: U1.pin25, LCD1.VSS, LCD1.LED-, LED1.green_anode, J1.pin5
  N15: U1.pin26, LCD1.VDD, R1.CW, J1.pin4, R5.Pin_1, R6.Pin_1, R7.Pin_0
  N16: U1.pin27, U1.pin51, SPKR1.pin1, RE2.EncoderPinC, RE3.EncoderPinC, RE1.EncoderPinC
  N17: U1.pin36, RE1.EncoderPinB
  N18: U1.pin37, RE1.EncoderPinA
  N19: U1.pin38, RE2.EncoderPinB
  N20: U1.pin39, RE2.EncoderPinA
  N21: U1.pin40, RE3.EncoderPinB
  N22: U1.pin41, RE3.EncoderPinA
  N23: U1.pin49, C1.+, R8.Pin_1
  N24: LCD1.V0, R1.WIPER
  N25: LCD1.LED+, R7.Pin_1
  N26: R2.Pin_1, LED1.common_cathode
  N27: R3.Pin_1, LED1.red_anode
  N28: R4.Pin_1, LED1.blue_anode
  N29: S1.Pin_1, S1.Pin_2
  N30: S1.Pin_3, S1.Pin_4
  N31: S2.Pin_1, S2.Pin_2
  N32: S2.Pin_3, S2.Pin_4
  N33: S3.Pin_1, S3.Pin_2
  N34: S3.Pin_3, S3.Pin_4
  N35: S4.Pin_1, S4.Pin_2
  N36: S4.Pin_3, S4.Pin_4
  N37: SPKR1.pin2, C1.-
  N38: R8.Pin_0, LED2.anode

notes:
  GND
  VCCIO
  Sequencer Board
  GND
  VDD
  SPI
