# Fritzing sketch Sequencer_Board_PSoC_5LP_Protokit_Test (saved by Fritzing 0.9.2b)
breadboards: 2
perfboards: 1

parts:
  U1 = mystery part, 52 pins [chip_label="PSoC 5LP Prototyping Kit"]
  R1 = Resistor [tolerance=±5% resistance=4.7k package=THT]
  R3 = Resistor [tolerance=±5% resistance=4.7k package=THT]
  LED1 = RGB LED (com. cathode, rgb) [package="5 mm [THT]"]
  R4 = Resistor [tolerance=±5% resistance=1.5k package=THT]
  R5 = Resistor [tolerance=±5% resistance=1k package=THT]
  R6 = Resistor [tolerance=±5% resistance=1k package=THT]
  J1 = female pin header, 5 pins [form="♀ (female)"]

nets:
  N1: U1.pin36, R3.Pin_0, J1.pin1
  N2: U1.pin37, R1.Pin_0, J1.pin2
  N3: U1.pin38, J1.pin3
  N4: U1.pin42, R4.Pin_1
  N5: U1.pin43, R6.Pin_1
  N6: U1.pin44, R5.Pin_1
  N7: U1.pin51, LED1.common_cathode, J1.pin5
  N8: U1.pin52, R1.Pin_1, R3.Pin_1, J1.pin4
  N9: LED1.red_anode, R4.Pin_0
  N10: LED1.green_anode, R5.Pin_0
  N11: LED1.blue_anode, R6.Pin_0

notes:
  Sequencer Board
