# Fritzing sketch MCP4922_PSoC4PioneerKit (saved by Fritzing 0.9.2b)
breadboards: 1
perfboards: 1

parts:
  U1 = mystery part, 14 pins [chip_label=MCP4922]
  R1 = Resistor [tolerance=±5% resistance=220 package=THT]
  LED1 = LED - 5mm [color="Red (633nm)" package="5 mm [THT]"]
  J1 = female pin header, 9 pins [form="♀ (female)"]
  J2 = female pin header, 8 pins [form="♀ (female)"]
  J3 = female pin header, 10 pins [form="♀ (female)"]
  J4 = female pin header, 8 pins [form="♀ (female)"]
  J5 = female pin header, 9 pins [form="♀ (female)"]  # not connected
  R2 = Resistor [tolerance=±5% resistance=220 package=THT]
  LED2 = LED - 5mm [color="Red (633nm)" package="5 mm [THT]"]
  C1 = Ceramic Capacitor [capacitance=100nF package="100 mil [THT, multilayer]"]
  C2 = Electrolytic Capacitor [capacitance=1µF package="100 mil [THT, electrolytic]"]

nets:
  N1: U1.pin1, U1.pin9, U1.pin11, U1.pin13, J2.pin4, C1.1, C2.+
  N2: U1.pin3, J4.pin6
  N3: U1.pin4, J3.pin5
  N4: U1.pin5, J4.pin8
  N5: U1.pin8, J1.pin7
  N6: U1.pin10, R2.Pin_1
  N7: U1.pin12, LED1.cathode, J2.pin6, LED2.cathode, C1.0, C2.-
  N8: U1.pin14, R1.Pin_1
  N9: R1.Pin_0, LED1.anode
  N10: R2.Pin_0, LED2.anode

notes:
  PSoC 4
  Pioneer Kit
