# Fritzing sketch MCP4922_PSoC4PioneerKit_SPI_Master_Compornent (saved by Fritzing 0.9.2b)
breadboards: 1
perfboards: 1

parts:
  U1 = mystery part, 14 pins [chip_label=MCP4922]
  J1 = female pin header, 1 pin [form="♀ (female)"]
  J2 = female pin header, 1 pin [form="♀ (female)"]
  J3 = female pin header, 10 pins [form="♀ (female)"]
  J4 = female pin header, 8 pins [form="♀ (female)"]
  J5 = female pin header, 8 pins [form="♀ (female)"]
  J6 = female pin header, 9 pins [form="♀ (female)"]
  J7 = female pin header, 9 pins [form="♀ (female)"]  # not connected

nets:
  N1: U1.pin1, J5.pin4
  N2: U1.pin3, J4.pin6
  N3: U1.pin4, J3.pin5
  N4: U1.pin5, J4.pin7
  N5: U1.pin8, J6.pin7
  N6: U1.pin9, U1.pin11, U1.pin13
  N7: U1.pin10, J2.pin1
  N8: U1.pin14, J1.pin1

notes:
  PSoC 4 Pioneer Kit
  ISR
  OV
