# Fritzing sketch PSoC 4 Pioneer Kit & Sequencer Board & SPLC792 & MCP4922 & REx3 (saved by Fritzing 0.9.2b)
perfboards: 2
breadboards: 2

parts:
  J1 = female pin header, 5 pins [form="♀ (female)"]
  J2 = female pin header, 8 pins [form="♀ (female)"]
  J4 = female pin header, 8 pins [form="♀ (female)"]
  J5 = female pin header, 10 pins [form="♀ (female)"]
  J6 = female pin header, 6 pins [form="♀ (female)"]  # not connected
  J7 = female pin header, 6 pins [form="♀ (female)"]  # not connected
  U2 = mystery part, 14 pins [chip_label=MCP4922]
  R3 = Resistor [tolerance=±5% resistance=220 package=THT]
  LED1 = LED - 5mm [color="Red (633nm)" package="5 mm [THT]"]
  C1 = Ceramic Capacitor [capacitance=100nF package="100 mil [THT, multilayer]"]
  C2 = Electrolytic Capacitor [capacitance=1µF package="100 mil [THT, electrolytic]"]
  U1 = mystery part, 9 pins [chip_label=SPLC792]
  R4 = Resistor [tolerance=±5% resistance=220 package=THT]
  RE2 = Rotary Encoder [package=THT]
  RE1 = Rotary Encoder [package=THT]
  J3 = female pin header, 9 pins [form="♀ (female)"]
  J8 = female pin header, 9 pins [form="♀ (female)"]
  RE3 = Rotary Encoder [package=THT]

nets:
  N1: J1.pin1, J2.pin6, U2.pin12, LED1.cathode, C1.0, C2.-, U1.pin2, U1.pin6, RE2.EncoderPinC, RE1.EncoderPinC
  N2: J1.pin2, J2.pin4, U2.pin1, U2.pin9, U2.pin11, U2.pin13, C1.1, C2.+, U1.pin9, R4.Pin_0
  N3: J1.pin3, J5.pin5, U1.pin3
  N4: J1.pin4, J5.pin1
  N5: J1.pin5, J5.pin2
  N6: J2.pin7, RE3.EncoderPinC
  N7: J4.pin7, U1.pin5
  N8: J4.pin8, U1.pin4
  N9: U2.pin3, J8.pin7
  N10: U2.pin4, J8.pin9
  N11: U2.pin8, J8.pin6
  N12: U2.pin14, R3.Pin_1
  N13: R3.Pin_0, LED1.anode
  N14: U1.pin1, R4.Pin_1
  N15: RE2.EncoderPinA, J3.pin1
  N16: RE2.EncoderPinB, J3.pin2
  N17: RE1.EncoderPinA, J3.pin3
  N18: RE1.EncoderPinB, J3.pin4
  N19: J3.pin5, RE3.EncoderPinB
  N20: J3.pin6, RE3.EncoderPinA

notes:
  PSoC 4 Pioneer Kit
  3.3V Drive
  Sequencer Board
  MCP4922
  1 VDD 8 ~LDAC
  2 NC 9 ~SHDN
  3 ~CS 10 VOUTB
  4 SCK 11 VREFB
  5 SDI 12 AVSS
  6 NC 13 VREFA
  7 NC 14 VOUTA
  TimerOV
  ISR
  IDAC8
