# Fritzing sketch PSoC 4 Pioneer Kit & Sequencer Board & SPLC792_I2C (saved by Fritzing 0.9.2b)
perfboards: 2
breadboards: 1

parts:
  J1 = female pin header, 5 pins [form="♀ (female)"]
  J2 = female pin header, 8 pins [form="♀ (female)"]
  J3 = double row female pin header, 10 pins [form="♀ (female)"]  # not connected
  J4 = female pin header, 8 pins [form="♀ (female)"]
  J5 = female pin header, 10 pins [form="♀ (female)"]
  J6 = female pin header, 6 pins [form="♀ (female)"]
  J7 = female pin header, 6 pins [form="♀ (female)"]
  U1 = mystery part, 9 pins [chip_label=SPLC792]
  R1 = Resistor [tolerance=±5% resistance=4.7k package=THT]
  R2 = Resistor [tolerance=±5% resistance=4.7k package=THT]

nets:
  N1: J1.pin1, J2.pin6, U1.pin6
  N2: J1.pin2, J2.pin4, U1.pin9, R1.Pin_0, R2.Pin_0
  N3: J1.pin3, J5.pin6, U1.pin3
  N4: J1.pin4, J5.pin1, U1.pin4, R2.Pin_1
  N5: J1.pin5, J5.pin2, U1.pin5, R1.Pin_1
  N6: J4.pin7, J6.pin2
  N7: J4.pin8, J7.pin2

notes:
  PSoC 4 Pioneer Kit
  Sequencer Board
